// Digital circuit control.dig as structural Verilog
module control (
  input  sys,
  input  [4:0] op,
  input  clock,
  input  t_in,
  output [2:0] aluop,
  output T,
  output halt,
  output error,
  output mem,
  output [1:0] memop,
  output jump
);

  wire and_2_out, and_3_out, halt_t, not_1_out, xor_1_out;
  wire [0:0] and_1_out;

  and and_1 (and_1_out[0], ~op[3], op[4], ~sys);  // And
  and and_2 (and_2_out, op[1], op[2], ~op[3], ~op[4]);  // And
  and and_3 (and_3_out, op[2], ~op[3], ~op[4]);  // And
  and and_4 (halt_t, op[0], ~op[1], sys);  // And
  Register u_T (.D(t_in), .C(clock), .en(1'b1), .Q(T));
  and and_5 (mem, ~sys, ~op[4], ~op[3], ~op[2]);  // And
  Multiplexer #(.Selector_Bits(2), .Bits(3)) multiplexer_1 (
    .sel({mem, and_1_out[0]}), .in_0(3'b111), .in_1(op[2:0]), .in_2(3'b000), .in_3(3'b000), .out(aluop));
  xor xor_1 (xor_1_out, op[0], T);
  not not_1 (not_1_out, T);
  Multiplexer multiplexer_2 (.sel(and_2_out), .in_0(and_3_out), .in_1(xor_1_out), .out(jump));
  and and_6 (halt, T, halt_t);
  and and_7 (error, halt_t, not_1_out);
  Multiplexer #(.Bits(2)) multiplexer_3 (.sel(mem), .in_0(2'b00), .in_1(op[1:0]), .out(memop));
endmodule
