// Digital circuit execute.dig as structural Verilog
module execute (
  input  [1:0] result_mux,
  input  [15:0] L,
  input  [15:0] R,
  output [15:0] result
);

  wire [15:0] add_1_s;

  Add #(.Bits(16)) add_1 (.a(L), .b(R), .c_i(1'b0), .s(add_1_s));  // open: c_o
  Multiplexer #(.Selector_Bits(2), .Bits(16)) multiplexer_1 (
    .sel(result_mux), .in_0(L), .in_1(add_1_s), .in_2(R), .in_3({16{1'b0}}), .out(result));
endmodule
