// Digital circuit frontpanel.dig as structural Verilog
module frontpanel (
  input  [7:0] value,
  input  [1:0] dest,
  input  [1:0] src,
  input  tworeg,
  output [31:0] R0,
  output [31:0] R1,
  output [31:0] R2,
  output [31:0] R3,
  output [3:0] PC
);

  wire add, add_out, advance_out, assembler_1_p9, assembler_1_p10, decoder_1_p1, decoder_1_p2, decoder_1_p6,
       execute_1_p4, fetch_1_p8, hex, hexdisplay_1_p2, hexdisplay_1_p4, hexdisplay_1_p6, hexdisplay_1_p7,
       hexdisplay_1_p9, hexdisplay_1_p11, hexdisplay_1_p14, hexdisplay_1_p16, hexdisplay_1_p19,
       hexdisplay_1_p21, hexdisplay_1_p23, hexdisplay_2_p2, hexdisplay_2_p4, hexdisplay_2_p7,
       hexdisplay_2_p9, hexdisplay_2_p11, hexdisplay_2_p14, hexdisplay_2_p16, instrdisplay_1_p1,
       instrdisplay_1_p2, instrdisplay_1_p3, instrdisplay_1_p4, instrdisplay_1_p5, instrdisplay_1_p6, jump,
       jump_out, L, mode_out, move, move_out, pmshim_1_p6, pmshim_1_p7, pmshim_1_p8, R, regdisplay_1_p1,
       regdisplay_1_p2, regdisplay_2_p1, regdisplay_2_p3, regdisplay_2_p5, regdisplay_2_p8, regdisplay_2_p12,
       rs, tworeg_t;
  wire [1:0] rd;
  wire [2:0] op;
  wire [3:0] hexdisplay_1_p1, hexdisplay_1_p3, hexdisplay_1_p5, hexdisplay_1_p8, hexdisplay_1_p10,
       hexdisplay_1_p13, hexdisplay_1_p15, hexdisplay_1_p17, hexdisplay_1_p20, hexdisplay_1_p22,
       hexdisplay_2_p1, hexdisplay_2_p3, hexdisplay_2_p5, hexdisplay_2_p8, hexdisplay_2_p10,
       hexdisplay_2_p13, hexdisplay_2_p15, hexdisplay_2_p17, pmshim_1_p4, regdisplay_2_p2, regdisplay_2_p4;
  wire [15:0] instrdisplay_1_d1, instrdisplay_1_d2, instrdisplay_1_d3, instrdisplay_1_d4, instrdisplay_1_d5,
       instrdisplay_1_d6, pmshim_1_p5, Program_d, regdisplay_1_d1, regdisplay_1_d2, regdisplay_2_p6,
       regdisplay_2_p10;

  Button u_add (.out(add_out));
  Button u_move (.out(move_out));
  Button u_jump (.out(jump_out));
  LED programming (.in(mode_out));
  DipSwitch mode (.out(mode_out));
  // assembler assembler_1: pin names not known; wires that end beside it: mode_out, value, dest, src, tworeg, add_out, move_out, jump_out, assembler_1_p9, assembler_1_p10
  SixteenSeg sixteenseg_1 (.led(regdisplay_1_d1), .dp(regdisplay_1_p1));
  regdisplay regdisplay_1 (
    .D1(regdisplay_1_d1), .P1(regdisplay_1_p1), .D2(regdisplay_1_d2), .P2(regdisplay_1_p2), .E(1'b1),
    .J(jump), .R(rd));
  SixteenSeg sixteenseg_2 (.led(regdisplay_1_d2), .dp(regdisplay_1_p2));
  DipSwitch u_hex (.out(hex));
  // pmshim pmshim_1: pin names not known; wires that end beside it: PC, assembler_1_p9, assembler_1_p10, pmshim_1_p4, pmshim_1_p5, pmshim_1_p6, pmshim_1_p7, pmshim_1_p8
  Seven_Seg_Hex seven_seg_hex_1 (.d(hexdisplay_1_p1), .dp(hexdisplay_1_p2));
  Seven_Seg_Hex seven_seg_hex_2 (.d(hexdisplay_1_p3), .dp(hexdisplay_1_p4));
  // hexdisplay hexdisplay_1: pin names not known; wires that end beside it: hexdisplay_1_p1, hexdisplay_1_p2, hexdisplay_1_p3, hexdisplay_1_p4, hexdisplay_1_p5, hexdisplay_1_p6, hexdisplay_1_p7, hexdisplay_1_p8, hexdisplay_1_p9, hexdisplay_1_p10, hexdisplay_1_p11, L, hexdisplay_1_p13, hexdisplay_1_p14, hexdisplay_1_p15, hexdisplay_1_p16, hexdisplay_1_p17, hex, hexdisplay_1_p19, hexdisplay_1_p20, hexdisplay_1_p21, hexdisplay_1_p22, hexdisplay_1_p23
  not not_1 (hexdisplay_1_p6, jump);
  EEPROMDualPort #(.AddrBits(4), .isProgramMemory("true"), .Bits(16)) Program (
    .A(pmshim_1_p4), .Din(pmshim_1_p5), .str(pmshim_1_p6), .C(pmshim_1_p7), .ld(pmshim_1_p8), .D(Program_d));
  Button advance (.out(advance_out));
  Seven_Seg_Hex seven_seg_hex_3 (.d(hexdisplay_1_p5), .dp(hexdisplay_1_p7));
  Seven_Seg_Hex seven_seg_hex_4 (.d(hexdisplay_1_p8), .dp(hexdisplay_1_p9));
  Seven_Seg_Hex seven_seg_hex_5 (.d(hexdisplay_1_p10), .dp(hexdisplay_1_p11));
  Seven_Seg_Hex seven_seg_hex_6 (.d(hexdisplay_1_p13), .dp(hexdisplay_1_p14));
  // fetch fetch_1: pin names not known; wires that end beside it: mode_out, assembler_1_p9, Program_d, advance_out, R, jump, PC, fetch_1_p8
  Seven_Seg_Hex seven_seg_hex_7 (.d(hexdisplay_1_p15), .dp(hexdisplay_1_p16));
  Seven_Seg_Hex seven_seg_hex_8 (.d(hexdisplay_1_p17), .dp(hexdisplay_1_p19));
  Seven_Seg_Hex seven_seg_hex_9 (.d(hexdisplay_1_p20), .dp(hexdisplay_1_p21));
  Seven_Seg_Hex seven_seg_hex_10 (.d(hexdisplay_1_p22), .dp(hexdisplay_1_p23));
  // decoder decoder_1: pin names not known; wires that end beside it: decoder_1_p1, decoder_1_p2, fetch_1_p8, rs, rd, decoder_1_p6, L, R, tworeg_t, move, add, op, jump
  SixteenSeg sixteenseg_3 (.led(instrdisplay_1_d1), .dp(instrdisplay_1_p1));
  instrdisplay instrdisplay_1 (
    .D1(instrdisplay_1_d1), .P1(instrdisplay_1_p1), .D2(instrdisplay_1_d2), .P2(instrdisplay_1_p2),
    .D3(instrdisplay_1_d3), .P3(instrdisplay_1_p3), .D4(instrdisplay_1_d4), .P4(instrdisplay_1_p4),
    .D5(instrdisplay_1_d5), .P5(instrdisplay_1_p5), .D6(instrdisplay_1_d6), .P6(instrdisplay_1_p6), .I(op));
  SixteenSeg sixteenseg_4 (.led(instrdisplay_1_d2), .dp(instrdisplay_1_p2));
  SixteenSeg sixteenseg_5 (.led(instrdisplay_1_d3), .dp(instrdisplay_1_p3));
  SixteenSeg sixteenseg_6 (.led(instrdisplay_1_d4), .dp(instrdisplay_1_p4));
  SixteenSeg sixteenseg_7 (.led(instrdisplay_1_d5), .dp(instrdisplay_1_p5));
  SixteenSeg sixteenseg_8 (.led(instrdisplay_1_d6), .dp(instrdisplay_1_p6));
  // execute execute_1: pin names not known; wires that end beside it: decoder_1_p6, L, R, execute_1_p4
  Seven_Seg_Hex seven_seg_hex_11 (.d(hexdisplay_2_p1), .dp(hexdisplay_2_p2));
  Seven_Seg_Hex seven_seg_hex_12 (.d(hexdisplay_2_p3), .dp(hexdisplay_2_p4));
  // hexdisplay hexdisplay_2: pin names not known; wires that end beside it: hexdisplay_2_p1, hexdisplay_2_p2, hexdisplay_2_p3, hexdisplay_2_p4, hexdisplay_2_p5, 1'b1, hexdisplay_2_p7, hexdisplay_2_p8, hexdisplay_2_p9, hexdisplay_2_p10, hexdisplay_2_p11, R, hexdisplay_2_p13, hexdisplay_2_p14, hexdisplay_2_p15, hexdisplay_2_p16, hexdisplay_2_p17, hex
  Seven_Seg_Hex seven_seg_hex_13 (.d(hexdisplay_2_p5), .dp(hexdisplay_2_p7));
  Seven_Seg_Hex seven_seg_hex_14 (.d(hexdisplay_2_p8), .dp(hexdisplay_2_p9));
  // regfile regfile_1: pin names not known; wires that end beside it: rs, rd, execute_1_p4, advance_out, decoder_1_p1, decoder_1_p2, R0, R1, R2, R3
  Seven_Seg_Hex seven_seg_hex_15 (.d(hexdisplay_2_p10), .dp(hexdisplay_2_p11));
  Seven_Seg_Hex seven_seg_hex_16 (.d(hexdisplay_2_p13), .dp(hexdisplay_2_p14));
  Seven_Seg_Hex seven_seg_hex_17 (.d(hexdisplay_2_p15), .dp(hexdisplay_2_p16));
  Seven_Seg_Hex seven_seg_hex_18 (.d(hexdisplay_2_p17), .dp(regdisplay_2_p1));
  Seven_Seg_Hex seven_seg_hex_19 (.d(regdisplay_2_p2), .dp(regdisplay_2_p3));
  Seven_Seg_Hex seven_seg_hex_20 (.d(regdisplay_2_p4), .dp(regdisplay_2_p5));
  SixteenSeg sixteenseg_9 (.led(regdisplay_2_p6), .dp(regdisplay_2_p8));
  // regdisplay regdisplay_2: pin names not known; wires that end beside it: regdisplay_2_p1, regdisplay_2_p2, regdisplay_2_p3, regdisplay_2_p4, regdisplay_2_p5, regdisplay_2_p6, tworeg_t, regdisplay_2_p8, 1'b0, regdisplay_2_p10, rs, regdisplay_2_p12
  SixteenSeg sixteenseg_10 (.led(regdisplay_2_p10), .dp(regdisplay_2_p12));

  // Notes on the sheet:
  //   rj45 Creates
  //   Fibonacci
  //   0: R2 = R2 + 1
  //   1: R2 = R2 + R1
  //   2: R3 = R2
  //   3: R1 = R1 + R2
  //   4: R3 = R1
  //   5: jump 1
  //   contents of Program (hex, n*v repeats v):
  //   120,161,1bd,191,17d,10e
endmodule
