// Digital circuit rj32.dig as structural Verilog
module rj32 (
  input  clock,
  input  step,
  input  run,
  input  [15:0] D_prog,
  input  [15:0] D_in,
  output [15:0] R0,
  output [15:0] R1,
  output [15:0] R2,
  output [15:0] R3,
  output [7:0] PC,
  output halt,
  output error,
  output skip,
  output rd_valid,
  output rs_valid,
  output [4:0] op,
  output [2:0] cond,
  output stall,
  output [15:0] L,
  output [15:0] R,
  output [1:0] rd,
  output [1:0] rs,
  output jump,
  output [7:0] A_prog,
  output clock_m,
  output [13:0] A_data,
  output [15:0] D_out,
  output w_en
);

  wire control_1_p4, control_1_p10, control_1_p11, control_1_p12, en;
  wire [2:0] control_1_p5;
  wire [15:0] execute_1_result, fetch_1_instr_o, memaccess_1_p2, memaccess_1_p7, regfile_1_rsval;

  not not_1 (clock_m, clock);
  fetch fetch_1 (
    .instr_i(D_prog), .clock(clock), .fetch(control_1_p12), .jump(jump), .value(R), .en(en),
    .instr_o(fetch_1_instr_o), .pc(A_prog));
  decoder decoder_1 (
    .rdval(memaccess_1_p2), .rsval(regfile_1_rsval), .instr(fetch_1_instr_o), .rs(rs), .rd(rd), .L(L), .R(R),
    .cond(cond), .op(op), .rs_valid(rs_valid), .rd_valid(rd_valid));
  clockctrl clockctrl_1 (.clock(clock), .step(step), .run(run), .stall(stall));
  // control control_1: pin names not known; wires that end beside it: op, stall, clock, control_1_p4, control_1_p5, skip, halt, error, en, control_1_p10, control_1_p11, control_1_p12, jump
  execute execute_1 (.L(L), .R(R), .cond(cond), .op(control_1_p5), .result(execute_1_result), .t_in(control_1_p4));
  // memaccess memaccess_1: pin names not known; wires that end beside it: execute_1_result, memaccess_1_p2, control_1_p10, control_1_p11, D_in, en, memaccess_1_p7, A_data, w_en, D_out
  regfile regfile_1 (
    .rs(rs), .rd(rd), .result(memaccess_1_p7), .clock(clock), .en(en), .rdval(memaccess_1_p2),
    .rsval(regfile_1_rsval), .R0(R0), .R1(R1), .R2(R2), .R3(R3));

  assign PC = A_prog;

  // Other names for the same wires on the sheet: A_data_t[13:0] = A_data; C = clock; cond_t[2:0] = cond;
  //   D_in_t[15:0] = D_in; D_out_t[15:0] = D_out; D_prog_t[15:0] = D_prog; error_t = error; halt_t = halt;
  //   jump_t = jump; L_t[15:0] = L; op_t[4:0] = op; A_prog_t[7:0] = A_prog; PC_t[7:0] = A_prog; R_t[15:0] = R;
  //   rd_t[1:0] = rd; rdvalid_t = rd_valid; rs_t[1:0] = rs; rsvalid_t = rs_valid; skip_t = skip; stall_t = stall;
  //   W_en_t = w_en

  // Notes on the sheet:
  //   clock: Hz: 10
  //   rj45 Creates
endmodule
