// Digital circuit vga_blinkenlights.dig as structural Verilog
module vga_blinkenlights (
  input  clock,
  input  [15:0] PC,
  input  [15:0] R0,
  input  [15:0] R1,
  input  [15:0] R2,
  input  [15:0] R3,
  input  [15:0] CD,
  output [3:0] R,
  output [3:0] G,
  output [3:0] B,
  output hs,
  output vs,
  output de,
  output [10:0] CA
);

  wire [6:0] PC_c_o, R0_c_o;
  wire [7:0] PC_cx_o, PC_cy_o, vga_display_1_cx, vga_display_1_cy;
  wire [11:0] PC_bg_o, PC_fg_o, R0_bg_o, R0_fg_o;

  vga_display vga_display_1 (
    .clock(clock), .res_H(12'h280), .fp_H(12'h10), .sync_H(12'h60), .bp_H(12'h30), .neg_H(1'b1),
    .res_V(12'h1e0), .fp_V(12'hb), .sync_V(12'h2), .bp_V(12'h21), .neg_V(1'b1), .char(R0_c_o), .fg(R0_fg_o),
    .bg(R0_bg_o), .CD(CD), .R(R), .G(G), .B(B), .hs(hs), .vs(vs), .de(de), .CX(vga_display_1_cx),
    .CY(vga_display_1_cy), .CA(CA));  // open: vblank, hblank
  vga_labelnum u_PC (
    .CX_i(vga_display_1_cx), .CY_i(vga_display_1_cy), .C_i({7{1'b0}}), .fg_i({12{1'b0}}), .bg_i({12{1'b0}}),
    .fg_lab(12'h1be), .fg_num(12'he07), .bg_c(12'h112), .CX_c(5'b00001), .CY_c(8'h2), .en(1'b1),
    .L_0(7'b0100000), .L_1(7'b1010000), .L_2(7'b1000011), .N(PC), .CX_o(PC_cx_o), .CY_o(PC_cy_o),
    .C_o(PC_c_o), .fg_o(PC_fg_o), .bg_o(PC_bg_o));  // open: busy
  vga_labelnum u_R0 (
    .CX_i(PC_cx_o), .CY_i(PC_cy_o), .C_i(PC_c_o), .fg_i(PC_fg_o), .bg_i(PC_bg_o), .fg_lab(12'h1be),
    .fg_num(12'he07), .bg_c(12'h112), .CX_c(5'b00001), .CY_c(8'h3), .en(1'b1), .L_0(7'b0100000),
    .L_1(7'b1010010), .L_2(7'b0110000), .N(R0), .C_o(R0_c_o), .fg_o(R0_fg_o), .bg_o(R0_bg_o));  // open: CX_o, CY_o, busy

  // Other names for the same wires on the sheet: C = clock; PC_t[15:0] = PC; R0_t[15:0] = R0; R1_t[15:0] = R1;
  //   R2_t[15:0] = R2; R3_t[15:0] = R3

  // Notes on the sheet:
  //   clock: Hz: 2147483647
endmodule
